# Fritzing sketch stepping_motor_M49SP-2K_ L298N_driver (saved by Fritzing 0.9.3b)

parts:
  M1 = Stepper Motor - Bipolar
  S1 = H-Bridge with L298N
  18650_holder1 = 18650 holder [package="DIP (Dual Inline) [THT]"]
  18650_holder2 = 18650 holder [package="DIP (Dual Inline) [THT]"]
  Part1 = Arduino Uno (Rev3)

nets:
  N1: M1.A, S1.M1-01
  N2: M1.C, S1.M1-02
  N3: M1.B, S1.M2-01
  N4: M1.D, S1.M2-02
  N5: S1.12V, 18650_holder1.holder_+
  GND: S1.GND, 18650_holder2.holder_-, Part1.GND
  5V: S1.5V, Part1.VIN
  N6: S1.ENA, Part1.D3_PWM
  N7: S1.IN1, Part1.D8
  N8: S1.IN2, Part1.D9_PWM
  N9: S1.IN3, Part1.D10_PWM/SS
  N10: S1.IN4, Part1.D11_PWM/MOSI
  N11: S1.ENB, Part1.D5_PWM
  N12: 18650_holder1.holder_-, 18650_holder2.holder_+

custom parts:
  H-Bridge with L298N: h-bridge
  18650 holder: Акум формата 18650 в холдере

// code stored in the sketch: stepping_motor_M49SP-2K_ L298N_driver.ino
#define in1 8
#define in2 9
#define in3 10
#define in4 11
#define enA 3 
#define enB 5

int dl = 50; //delay time

void setup() {
  pinMode(in1, OUTPUT);
  pinMode(in2, OUTPUT);
  pinMode(in3, OUTPUT);
  pinMode(in4, OUTPUT);
  pinMode(enA, OUTPUT);
  pinMode(enB, OUTPUT);
  analogWrite(enA, 255);
  analogWrite(enB, 255);
}

void loop() {
  digitalWrite(in1, HIGH); 
  digitalWrite(in2, LOW); 
  digitalWrite(in3, LOW); 
  digitalWrite(in4, HIGH); 
  delay(dl);
  digitalWrite(in1, HIGH); 
  digitalWrite(in2, HIGH); 
  digitalWrite(in3, LOW); 
  digitalWrite(in4, LOW); 
  delay(dl);
  digitalWrite(in1, LOW); 
  digitalWrite(in2, HIGH); 
  digitalWrite(in3, HIGH); 
  digitalWrite(in4, LOW); 
  delay(dl);
  digitalWrite(in1, LOW); 
  digitalWrite(in2, LOW); 
  digitalWrite(in3, HIGH); 
  digitalWrite(in4, HIGH); 
  delay(dl);
}
